// Logisim project control_logic.circ as structural Verilog: 1 circuit, main circuit control_logic
module control_logic (
  input  [31:0] inst,
  input  BrEq,
  input  BrLt,
  output PCSel,
  output RegWEn,
  output [2:0] ImmSel,
  output BrUn,
  output ASel,
  output BSel,
  output [3:0] ALUSel,
  output MemRW,
  output [1:0] WBSel,
  output CSRSel,
  output CSRWen
);

  wire Alu_port, and1, and_1_out, and_2_out, and_3_out, and_4_out, and_5_out, and_6_out, and_7_out,
       and_8_out, and_9_out, and_10_out, and_11_out, and_12_out, and_13_out, and_14_out, and_15_out,
       and_16_out, and_17_out, and_18_out, and_19_out, and_20_out, and_22_out, and_23_out, bsel13,
       comparator_7_eq, comparator_8_eq, comparator_9_eq, comparator_10_eq, comparator_11_eq,
       comparator_12_eq, comparator_17_eq, comparator_18_eq, comparator_19_eq, comparator_20_eq,
       comparator_21_eq, comparator_22_eq, comparator_23_eq, comparator_24_eq, comparator_25_eq,
       comparator_26_eq, comparator_27_eq, comparator_28_eq, comparator_29_eq, comparator_30_eq,
       comparator_31_eq, comparator_32_eq, comparator_33_eq, comparator_34_eq, comparator_35_eq,
       comparator_36_eq, comparator_37_eq, comparator_38_eq, comparator_40_eq, comparator_41_eq,
       comparator_42_eq, comparator_43_eq, comparator_44_eq, comparator_45_eq, comparator_46_eq,
       comparator_47_eq, comparator_48_eq, comparator_49_eq, comparator_50_eq, comparator_51_eq,
       comparator_52_eq, I_type_addr, I_type_arith, I_type_jalr, mul10, mulh14, mulhu11, not_1_out,
       not_2_out, not_3_out, not_4_out, or2, or_1_out, or_2_out, or_3_out, or_4_out, or_6_out, or_7_out,
       or_8_out, Pcp4_port, Rtype, SBtype, sll6, slt7, sra5, srl4, sub12, U_type_auipc, UJtype, xor3;

  Comparator #(.width(7)) comparator_1 (.a(inst[6:0]), .b(7'b1100011), .eq(SBtype));  // open: gt, lt
  Comparator #(.width(7)) comparator_2 (.a(inst[6:0]), .b(7'b0110011), .eq(Rtype));  // open: gt, lt
  Comparator #(.width(7)) comparator_3 (.a(inst[6:0]), .b(7'b0010011), .eq(I_type_arith));  // open: gt, lt
  Comparator #(.width(7)) comparator_4 (.a(inst[6:0]), .b(7'b0000011), .eq(I_type_addr));  // open: gt, lt
  Comparator #(.width(7)) comparator_5 (.a(inst[6:0]), .b(7'b1100111), .eq(I_type_jalr));  // open: gt, lt
  Comparator #(.width(7)) comparator_6 (.a(inst[6:0]), .b(7'b1110011), .eq(CSRWen));  // open: gt, lt
  Comparator #(.width(3)) comparator_7 (.a(inst[14:12]), .b(3'b000), .eq(comparator_7_eq));  // open: gt, lt
  Comparator #(.width(3)) comparator_8 (.a(inst[14:12]), .b(3'b001), .eq(comparator_8_eq));  // open: gt, lt
  Comparator #(.width(3)) comparator_9 (.a(inst[14:12]), .b(3'b100), .eq(comparator_9_eq));  // open: gt, lt
  Comparator #(.width(3)) comparator_10 (.a(inst[14:12]), .b(3'b101), .eq(comparator_10_eq));  // open: gt, lt
  Comparator #(.width(3)) comparator_11 (.a(inst[14:12]), .b(3'b110), .eq(comparator_11_eq));  // open: gt, lt
  Comparator #(.width(3)) comparator_12 (.a(inst[14:12]), .b(3'b111), .eq(comparator_12_eq));  // open: gt, lt
  not not_1 (not_1_out, BrEq);
  not not_2 (not_2_out, BrLt);
  not not_3 (not_3_out, BrLt);
  and and_1 (and_1_out, comparator_7_eq, SBtype, BrEq);
  and and_2 (and_2_out, comparator_8_eq, SBtype, not_1_out);
  and and_3 (and_3_out, comparator_9_eq, SBtype, BrLt);
  and and_4 (and_4_out, comparator_10_eq, SBtype, not_2_out);
  and and_5 (and_5_out, comparator_11_eq, SBtype, BrLt);
  and and_6 (and_6_out, comparator_12_eq, SBtype, not_3_out);
  or or_1 (or_1_out, I_type_addr, I_type_arith, I_type_jalr);
  or or_2 (or_2_out, U_type_auipc, bsel13);
  Comparator #(.width(7)) comparator_13 (.a(inst[6:0]), .b(7'b1101111), .eq(UJtype));  // open: gt, lt
  Comparator #(.width(7)) comparator_14 (.a(inst[6:0]), .b(7'b0100011), .eq(MemRW));  // open: gt, lt
  Comparator #(.width(7)) comparator_15 (.a(inst[6:0]), .b(7'b0010111), .eq(U_type_auipc));  // open: gt, lt
  Comparator #(.width(7)) comparator_16 (.a(inst[6:0]), .b(7'b0110111), .eq(bsel13));  // open: gt, lt
  Priority_Encoder priority_encoder_1 (
    .in0(1'b1), .in1(or_1_out), .in2(MemRW), .in3(SBtype), .in4(or_2_out), .in5(UJtype), .out(ImmSel));  // open: in6, in7, en_in, gs, en_out
  or or_3 (or_3_out, UJtype, I_type_jalr);
  or or_4 (or_4_out, and_1_out, and_2_out, and_3_out, and_4_out, and_5_out, and_6_out);
  or or_5 (PCSel, or_3_out, or_4_out);
  Comparator #(.width(3)) comparator_17 (.a(inst[14:12]), .b(3'b111), .eq(comparator_17_eq));  // open: gt, lt
  Comparator #(.width(7)) comparator_18 (.a(inst[31:25]), .b({7{1'b0}}), .eq(comparator_18_eq));  // open: gt, lt
  Comparator #(.width(3)) comparator_19 (.a(inst[14:12]), .b(3'b110), .eq(comparator_19_eq));  // open: gt, lt
  Comparator #(.width(7)) comparator_20 (.a(inst[31:25]), .b({7{1'b0}}), .eq(comparator_20_eq));  // open: gt, lt
  Comparator #(.width(3)) comparator_21 (.a(inst[14:12]), .b(3'b100), .eq(comparator_21_eq));  // open: gt, lt
  Comparator #(.width(7)) comparator_22 (.a(inst[31:25]), .b({7{1'b0}}), .eq(comparator_22_eq));  // open: gt, lt
  Comparator #(.width(3)) comparator_23 (.a(inst[14:12]), .b(3'b101), .eq(comparator_23_eq));  // open: gt, lt
  Comparator #(.width(7)) comparator_24 (.a(inst[31:25]), .b({7{1'b0}}), .eq(comparator_24_eq));  // open: gt, lt
  Comparator #(.width(3)) comparator_25 (.a(inst[14:12]), .b(3'b101), .eq(comparator_25_eq));  // open: gt, lt
  Comparator #(.width(3)) comparator_26 (.a(inst[14:12]), .b(3'b101), .eq(comparator_26_eq));  // open: gt, lt
  Comparator #(.width(7)) comparator_27 (.a(inst[31:25]), .b(7'b0100000), .eq(comparator_27_eq));  // open: gt, lt
  Comparator #(.width(3)) comparator_28 (.a(inst[14:12]), .b(3'b101), .eq(comparator_28_eq));  // open: gt, lt
  Comparator #(.width(3)) comparator_29 (.a(inst[14:12]), .b(3'b010), .eq(comparator_29_eq));  // open: gt, lt
  Comparator #(.width(7)) comparator_30 (.a(inst[31:25]), .b({7{1'b0}}), .eq(comparator_30_eq));  // open: gt, lt
  Comparator #(.width(3)) comparator_31 (.a(inst[14:12]), .b(3'b111), .eq(comparator_31_eq));  // open: gt, lt
  Comparator #(.width(3)) comparator_32 (.a(inst[14:12]), .b(3'b110), .eq(comparator_32_eq));  // open: gt, lt
  Comparator #(.width(3)) comparator_33 (.a(inst[14:12]), .b(3'b100), .eq(comparator_33_eq));  // open: gt, lt
  Comparator #(.width(7)) comparator_34 (.a(inst[31:25]), .b({7{1'b0}}), .eq(comparator_34_eq));  // open: gt, lt
  Comparator #(.width(7)) comparator_35 (.a(inst[31:25]), .b(7'b0100000), .eq(comparator_35_eq));  // open: gt, lt
  Comparator #(.width(3)) comparator_36 (.a(inst[14:12]), .b(3'b010), .eq(comparator_36_eq));  // open: gt, lt
  or or_6 (or_6_out, I_type_addr, I_type_arith);
  or or_7 (or_7_out, UJtype, I_type_jalr);
  and and_7 (and_7_out, Rtype, comparator_17_eq, comparator_18_eq);
  and and_8 (and_8_out, I_type_arith, comparator_31_eq);
  and and_9 (and_9_out, Rtype, comparator_19_eq, comparator_20_eq);
  and and_10 (and_10_out, I_type_arith, comparator_32_eq);
  and and_11 (and_11_out, Rtype, comparator_21_eq, comparator_22_eq);
  and and_12 (and_12_out, I_type_arith, comparator_33_eq);
  and and_13 (and_13_out, Rtype, comparator_23_eq, comparator_24_eq);
  and and_14 (and_14_out, I_type_arith, comparator_25_eq, comparator_34_eq);
  and and_15 (and_15_out, Rtype, comparator_26_eq, comparator_27_eq);
  and and_16 (and_16_out, I_type_arith, comparator_28_eq, comparator_35_eq);
  and and_17 (and_17_out, Rtype, comparator_29_eq, comparator_30_eq);
  and and_18 (and_18_out, I_type_arith, comparator_36_eq);
  or or_8 (or_8_out, U_type_auipc, bsel13);
  not not_4 (not_4_out, I_type_jalr);
  or or_9 (and1, and_7_out, and_8_out);
  or or_10 (or2, and_9_out, and_10_out);
  or or_11 (xor3, and_11_out, and_12_out);
  or or_12 (srl4, and_13_out, and_14_out);
  or or_13 (sra5, and_15_out, and_16_out);
  or or_14 (slt7, and_17_out, and_18_out);
  or or_15 (RegWEn, or_8_out, Rtype, or_6_out, or_7_out);
  Comparator #(.width(3)) comparator_37 (.a(inst[14:12]), .b(3'b110), .eq(comparator_37_eq));  // open: gt, lt
  Comparator #(.width(3)) comparator_38 (.a(inst[14:12]), .b(3'b111), .eq(comparator_38_eq));  // open: gt, lt
  and and_19 (and_19_out, comparator_37_eq, SBtype);
  and and_20 (and_20_out, comparator_38_eq, SBtype);
  and and_21 (ASel, PCSel, not_4_out);
  Comparator #(.mode("unsigned"), .width(3)) comparator_39 (.a(ImmSel), .b(3'b000), .gt(BSel));  // open: eq, lt
  or or_16 (BrUn, and_19_out, and_20_out);
  Comparator #(.width(3)) comparator_40 (.a(inst[14:12]), .b(3'b000), .eq(comparator_40_eq));  // open: gt, lt
  Comparator #(.width(7)) comparator_41 (.a(inst[31:25]), .b(7'b0000001), .eq(comparator_41_eq));  // open: gt, lt
  Comparator #(.width(3)) comparator_42 (.a(inst[14:12]), .b(3'b011), .eq(comparator_42_eq));  // open: gt, lt
  Comparator #(.width(7)) comparator_43 (.a(inst[31:25]), .b(7'b0000001), .eq(comparator_43_eq));  // open: gt, lt
  Comparator #(.width(3)) comparator_44 (.a(inst[14:12]), .b(3'b000), .eq(comparator_44_eq));  // open: gt, lt
  Comparator #(.width(7)) comparator_45 (.a(inst[31:25]), .b(7'b0100000), .eq(comparator_45_eq));  // open: gt, lt
  Comparator #(.width(3)) comparator_46 (.a(inst[14:12]), .b(3'b001), .eq(comparator_46_eq));  // open: gt, lt
  Comparator #(.width(7)) comparator_47 (.a(inst[31:25]), .b(7'b0000001), .eq(comparator_47_eq));  // open: gt, lt
  Comparator #(.width(3)) comparator_48 (.a(inst[14:12]), .b(3'b001), .eq(comparator_48_eq));  // open: gt, lt
  Comparator #(.width(7)) comparator_49 (.a(inst[31:25]), .b({7{1'b0}}), .eq(comparator_49_eq));  // open: gt, lt
  Comparator #(.width(3)) comparator_50 (.a(inst[14:12]), .b(3'b001), .eq(comparator_50_eq));  // open: gt, lt
  Comparator #(.width(7)) comparator_51 (.a(inst[31:25]), .b({7{1'b0}}), .eq(comparator_51_eq));  // open: gt, lt
  Priority_Encoder #(.select(4)) priority_encoder_2 (
    .in0(1'b1), .in1(and1), .in2(or2), .in3(xor3), .in4(srl4), .in5(sra5), .in6(sll6), .in7(slt7),
    .in10(mul10), .in11(mulhu11), .in12(sub12), .in13(bsel13), .in14(mulh14), .out(ALUSel));  // open: in8, in9, in15, gs, en_out, en_in
  and and_22 (and_22_out, Rtype, comparator_48_eq, comparator_49_eq);
  and and_23 (and_23_out, I_type_arith, comparator_50_eq, comparator_51_eq);
  and and_24 (mul10, Rtype, comparator_40_eq, comparator_41_eq);
  and and_25 (mulhu11, Rtype, comparator_42_eq, comparator_43_eq);
  and and_26 (sub12, Rtype, comparator_44_eq, comparator_45_eq);
  and and_27 (mulh14, Rtype, comparator_46_eq, comparator_47_eq);
  or or_17 (sll6, and_22_out, and_23_out);
  or or_18 (Alu_port, Rtype, I_type_arith, U_type_auipc, bsel13);
  or or_19 (Pcp4_port, I_type_jalr, UJtype);
  Comparator #(.width(3)) comparator_52 (.a(inst[14:12]), .b(3'b001), .eq(comparator_52_eq));  // open: gt, lt
  and and_28 (CSRSel, CSRWen, comparator_52_eq);
  Priority_Encoder #(.select(2)) priority_encoder_3 (
    .in0(I_type_addr), .in1(Alu_port), .in2(Pcp4_port), .out(WBSel));  // open: in3, gs, en_out, en_in

  // Other names for the same wires on the sheet: U_type_lui = bsel13; I_type_csr = CSRWen; opcode[6:0] = inst[6:0];
  //   func3[2:0] = inst[14:12]; func7[6:0] = inst[31:25]; Mem_port = I_type_addr; Stype = MemRW

  // Notes on the sheet:
  //   SB type
  //   R type
  //   I type Arith
  //   I type Addr
  //   I type jalr
  //   I type Csr
  //   beq
  //   bne
  //   blt
  //   bge
  //   bltu
  //   bgeu
  //   INPUTS to your circuit
  //   Inst Type Analyser
  //   UJ type jal
  //   S type
  //   U type auipc
  //   U type lui
  //   Branch Inst(SB_type)
  //   ImmSel Part
  //   Inst fields
  //   PCSel circuits.
  //   Jump Inst
  //   ImmSel > 0: select Imm
  //   DON'T CHANGE THE LOCATIONS OF THE INPUTS AND OUTPUTS!
  //   OUTPUT from your circuit
  //   bltu
  //   bgeu
  //   RegWen circuit
  //   BrUn circuit
  //   ASel & BSel circuit
  //   ALUSel Part
  //   ALUSel should always be set to 0 for addition, and exception cases should be added if needed.
  //   CSRSel circuit
  //   WBSel circuit
  //   csrw: 1, csrwi: 0
endmodule
