// Logisim project cpu.circ as structural Verilog: 1 circuit, main circuit cpu
module cpu (
  input  clk,
  input  [31:0] INSTRUCTION,
  input  [31:0] READ_DATA,
  output [31:0] WRITE_ADDRESS,
  output [31:0] PROGRAM_COUNTER,
  output [31:0] ra,
  output [31:0] sp,
  output [31:0] t0,
  output [31:0] t1,
  output [31:0] t2,
  output [31:0] s0,
  output [31:0] s1,
  output [31:0] a0,
  output [31:0] tohost,
  output [3:0] WRITE_ENABLE,
  output [31:0] WRITE_DATA
);

  wire ASel, BrEq, BrLt, BrUn, BSel, comparator_1_eq, CSRSel, CSRWen, MemRW, PCSel, RegWEn;
  wire [1:0] WBSel;
  wire [2:0] ImmSel;
  wire [3:0] ALUSel, multiplexer_9_out;
  wire [31:0] adder_1_out, adder_2_out, bit_extender_1_out, Imm, INSTRUCTION1, multiplexer_1_out,
       multiplexer_2_out, multiplexer_3_out, multiplexer_4_out, multiplexer_5_out, multiplexer_6_out,
       multiplexer_7_out, multiplexer_8_out, PROGRAM_COUNTER1, Read_Data_1, READ_DATA_Final;

  Adder #(.width(32)) adder_1 (.a(PROGRAM_COUNTER), .b(32'h4), .out(adder_1_out));  // open: cin, cout
  Register #(.width(32)) PC (.D(multiplexer_1_out), .clk(clk), .Q(PROGRAM_COUNTER));  // open: en, clr
  Multiplexer #(.enable("false"), .width(32)) multiplexer_1 (
    .in0(adder_1_out), .in1(WRITE_ADDRESS), .out(multiplexer_1_out), .sel(PCSel));
  Register #(.width(32)) register_1 (.D(PROGRAM_COUNTER), .clk(clk), .Q(PROGRAM_COUNTER1));  // open: en, clr
  Register #(.width(32)) stage (.D(multiplexer_2_out), .clk(clk), .Q(INSTRUCTION1));  // open: en, clr
  Multiplexer #(.enable("false"), .width(32)) multiplexer_2 (
    .in0(INSTRUCTION), .in1(32'h13), .out(multiplexer_2_out), .sel(PCSel));
  imm_gen imm_gen_1 (.inst(INSTRUCTION1), .ImmSel(ImmSel), .imm(Imm));
  branch_comp branch_comp_1 (.rs1(Read_Data_1), .rs2(WRITE_DATA), .BrUn(BrUn), .BrEq(BrEq), .BrLt(BrLt));
  Adder #(.width(32)) adder_2 (.a(PROGRAM_COUNTER1), .b(32'h4), .out(adder_2_out));  // open: cin, cout
  Multiplexer #(.enable("false"), .select(2), .width(32)) multiplexer_3 (
    .in0(READ_DATA_Final), .in1(WRITE_ADDRESS), .in2(adder_2_out), .out(multiplexer_3_out), .sel(WBSel));  // open: in3
  control_logic control_logic_1 (
    .CSRWen(CSRWen), .PCSel(PCSel), .RegWEn(RegWEn), .ImmSel(ImmSel), .BrUn(BrUn), .ASel(ASel), .BSel(BSel),
    .ALUSel(ALUSel), .MemRW(MemRW), .WBSel(WBSel), .CSRSel(CSRSel), .inst(INSTRUCTION1), .BrEq(BrEq),
    .BrLt(BrLt));
  regfile regfile_1 (
    .rs1(INSTRUCTION1[19:15]), .rs2(INSTRUCTION1[24:20]), .rd(INSTRUCTION1[11:7]),
    .Write_Data(multiplexer_3_out), .RegWEn(RegWEn), .clk(clk), .ra(ra), .sp(sp), .t0(t0), .t1(t1), .t2(t2),
    .s0(s0), .s1(s1), .a0(a0), .Read_Data_1(Read_Data_1), .Read_Data_2(WRITE_DATA));
  Multiplexer #(.enable("false"), .select(2), .width(32)) multiplexer_4 (
    .in0(32'hff), .in1(32'hffff), .in2({32{1'b1}}), .out(multiplexer_4_out), .sel(INSTRUCTION1[13:12]));  // open: in3
  Comparator #(.width(7)) comparator_1 (.a(INSTRUCTION1[6:0]), .b(7'b0000011), .eq(comparator_1_eq));  // open: gt, lt
  Multiplexer #(.enable("false"), .width(32)) multiplexer_5 (
    .in0({32{1'b0}}), .in1(multiplexer_4_out), .out(multiplexer_5_out), .sel(comparator_1_eq));
  Multiplexer #(.enable("false"), .width(32)) multiplexer_6 (
    .in0(WRITE_DATA), .in1(Imm), .out(multiplexer_6_out), .sel(BSel));
  assign READ_DATA_Final = multiplexer_5_out & READ_DATA;  // AND_Gate and_1, 32 bits wide
  Multiplexer #(.enable("false"), .width(32)) multiplexer_7 (
    .in0(Read_Data_1), .in1(PROGRAM_COUNTER1), .out(multiplexer_7_out), .sel(ASel));
  assign bit_extender_1_out = {{27{1'b0}}, INSTRUCTION1[19:15]};  // Bit_Extender bit_extender_1
  Multiplexer #(.enable("false"), .width(32)) multiplexer_8 (
    .in0(bit_extender_1_out), .in1(Read_Data_1), .out(multiplexer_8_out), .sel(CSRSel));
  alu alu_1 (.Result(WRITE_ADDRESS), .A(multiplexer_7_out), .B(multiplexer_6_out), .ALUSel(ALUSel));
  Multiplexer #(.enable("false"), .select(2), .width(4)) multiplexer_9 (
    .in0(4'b0001), .in1(4'b0011), .in2(4'b1111), .out(multiplexer_9_out), .sel(INSTRUCTION1[13:12]));  // open: in3
  csr csr_1 (
    .CSR_address(INSTRUCTION1[31:20]), .CSR_din(multiplexer_8_out), .CSR_WE(CSRWen), .clk(clk),
    .tohost(tohost));
  Multiplexer #(.enable("false"), .width(4)) multiplexer_10 (
    .in0(4'b0000), .in1(multiplexer_9_out), .out(WRITE_ENABLE), .sel(MemRW));

  // Other names for the same wires on the sheet: ALUResult[31:0] = WRITE_ADDRESS; Read_Data_2[31:0] = WRITE_DATA

  // Notes on the sheet:
  //   Output to IMEM
  //   IMEM (do **NOT** move this)
  //   Inputs from IMEM
  //   It is OK to move the PC, RegFile, ALU, MEM, Branch Comp, Imm Gen, and Control Logic to wherever is most convenient for you when constructing your CPU, and to delete this text
  //   Inputs/Outputs for testing. Do **NOT** move these.
  //   Outputs To DMEM
  //   DMEM (do **NOT** move this)
  //   Inputs From DMEM
endmodule
