// Logisim project imm_gen.circ as structural Verilog: 1 circuit, main circuit imm_gen
module imm_gen (
  input  [31:0] inst,
  input  [2:0] ImmSel,
  output [31:0] imm
);

  assign imm = {{20{1'b0}}, inst[31:20]};  // Bit_Extender bit_extender_1

  // Notes on the sheet:
  //   INPUTS to your circuit
  //   Case1: I-type instruction imm[11:0]
  //   DON'T CHANGE THE LOCATIONS OF THE INPUTS AND OUTPUTS!
  //   OUTPUT from your circuit
endmodule
