// Logisim project regfile.circ as structural Verilog: 1 circuit, main circuit regfile
module regfile (
  input  [4:0] rs1,
  input  [4:0] rs2,
  input  [4:0] rd,
  input  [31:0] Write_Data,
  input  RegWEn,
  input  clk,
  output [31:0] ra,
  output [31:0] sp,
  output [31:0] t0,
  output [31:0] t1,
  output [31:0] t2,
  output [31:0] s0,
  output [31:0] s1,
  output [31:0] a0,
  output [31:0] Read_Data_1,
  output [31:0] Read_Data_2
);

  wire decoder_1_out1, decoder_1_out2, decoder_1_out3, decoder_1_out4, decoder_1_out5, decoder_1_out6,
       decoder_1_out7, decoder_1_out8, decoder_1_out9, decoder_1_out10, decoder_1_out11, decoder_1_out12,
       decoder_1_out13, decoder_1_out14, decoder_1_out15, decoder_1_out16, decoder_1_out17, decoder_1_out18,
       decoder_1_out19, decoder_1_out20, decoder_1_out22, decoder_1_out23, decoder_1_out24, decoder_1_out25,
       decoder_1_out26, decoder_1_out27, decoder_1_out28, decoder_1_out29, decoder_1_out30, decoder_1_out31;
  wire [31:0] multiplexer_2_out, multiplexer_3_out, multiplexer_4_out, multiplexer_6_out, multiplexer_7_out,
       multiplexer_8_out, multiplexer_9_out, multiplexer_10_out, multiplexer_11_out, multiplexer_12_out,
       multiplexer_13_out, multiplexer_14_out, multiplexer_15_out, multiplexer_16_out, multiplexer_17_out,
       multiplexer_18_out, multiplexer_19_out, multiplexer_20_out, multiplexer_21_out, multiplexer_22_out,
       multiplexer_23_out, multiplexer_24_out, multiplexer_25_out, multiplexer_26_out, multiplexer_27_out,
       multiplexer_28_out, multiplexer_29_out, multiplexer_30_out, multiplexer_31_out, multiplexer_32_out,
       multiplexer_33_out, register_1_q, register_2_q, register_3_q, register_4_q, register_5_q,
       register_6_q, register_7_q, register_8_q, register_9_q, register_10_q, register_11_q, register_12_q,
       register_13_q, register_14_q, register_15_q, register_16_q, register_17_q, register_18_q,
       register_19_q, register_20_q, register_21_q, x0_q, x3_q, x4_q;

  Decoder #(.select(5)) decoder_1 (
    .out1(decoder_1_out1), .out2(decoder_1_out2), .out3(decoder_1_out3), .out4(decoder_1_out4),
    .out5(decoder_1_out5), .out6(decoder_1_out6), .out7(decoder_1_out7), .out8(decoder_1_out8),
    .out9(decoder_1_out9), .out10(decoder_1_out10), .out11(decoder_1_out11), .out12(decoder_1_out12),
    .out13(decoder_1_out13), .out14(decoder_1_out14), .out15(decoder_1_out15), .out16(decoder_1_out16),
    .out17(decoder_1_out17), .out18(decoder_1_out18), .out19(decoder_1_out19), .out20(decoder_1_out20),
    .out21(decoder_1_out20), .out22(decoder_1_out22), .out23(decoder_1_out23), .out24(decoder_1_out24),
    .out25(decoder_1_out25), .out26(decoder_1_out26), .out27(decoder_1_out27), .out28(decoder_1_out28),
    .out29(decoder_1_out29), .out30(decoder_1_out30), .out31(decoder_1_out31), .sel(rd));  // open: out0, en
  Register #(.width(32)) x0 (.D({32{1'b0}}), .en(RegWEn), .clk(clk), .Q(x0_q));  // open: clr
  Multiplexer #(.enable("false"), .select(5), .width(32)) multiplexer_1 (
    .in0(x0_q), .in1(ra), .in2(sp), .in3(x3_q), .in4(x4_q), .in5(t0), .in6(t1), .in7(t2), .in8(s0), .in9(s1),
    .in10(a0), .in11(register_12_q), .in12(register_14_q), .in13(register_16_q), .in14(register_18_q),
    .in15(register_20_q), .in16(register_1_q), .in17(register_2_q), .in18(register_3_q), .in19(register_4_q),
    .in20(register_5_q), .in21(register_6_q), .in22(register_7_q), .in23(register_8_q), .in24(register_9_q),
    .in25(register_10_q), .in26(register_11_q), .in27(register_13_q), .in28(register_15_q),
    .in29(register_17_q), .in30(register_19_q), .in31(register_21_q), .out(Read_Data_1), .sel(rs1));
  Register #(.width(32)) register_1 (.D(multiplexer_2_out), .en(RegWEn), .clk(clk), .Q(register_1_q));  // open: clr
  Multiplexer #(.enable("false"), .width(32)) multiplexer_2 (
    .in0(register_1_q), .in1(Write_Data), .out(multiplexer_2_out), .sel(decoder_1_out16));
  Register #(.width(32)) x1 (.D(multiplexer_3_out), .en(RegWEn), .clk(clk), .Q(ra));  // open: clr
  Multiplexer #(.enable("false"), .width(32)) multiplexer_3 (
    .in0(ra), .in1(Write_Data), .out(multiplexer_3_out), .sel(decoder_1_out1));
  Multiplexer #(.enable("false"), .width(32)) multiplexer_4 (
    .in0(register_2_q), .in1(Write_Data), .out(multiplexer_4_out), .sel(decoder_1_out17));
  Register #(.width(32)) register_2 (.D(multiplexer_4_out), .en(RegWEn), .clk(clk), .Q(register_2_q));  // open: clr
  Multiplexer #(.enable("false"), .select(5), .width(32)) multiplexer_5 (
    .in0(x0_q), .in1(ra), .in2(sp), .in3(x3_q), .in4(x4_q), .in5(t0), .in6(t1), .in7(t2), .in8(s0), .in9(s1),
    .in10(a0), .in11(register_12_q), .in12(register_14_q), .in13(register_16_q), .in14(register_18_q),
    .in15(register_20_q), .in16(register_1_q), .in17(register_2_q), .in18(register_3_q), .in19(register_4_q),
    .in20(register_5_q), .in21(register_6_q), .in22(register_7_q), .in23(register_8_q), .in24(register_9_q),
    .in25(register_10_q), .in26(register_11_q), .in27(register_13_q), .in28(register_15_q),
    .in29(register_17_q), .in30(register_19_q), .in31(register_21_q), .out(Read_Data_2), .sel(rs2));
  Register #(.width(32)) x2 (.D(multiplexer_6_out), .en(RegWEn), .clk(clk), .Q(sp));  // open: clr
  Multiplexer #(.enable("false"), .width(32)) multiplexer_6 (
    .in0(sp), .in1(Write_Data), .out(multiplexer_6_out), .sel(decoder_1_out2));
  Register #(.width(32)) register_3 (.D(multiplexer_7_out), .en(RegWEn), .clk(clk), .Q(register_3_q));  // open: clr
  Multiplexer #(.enable("false"), .width(32)) multiplexer_7 (
    .in0(register_3_q), .in1(Write_Data), .out(multiplexer_7_out), .sel(decoder_1_out18));
  Multiplexer #(.enable("false"), .width(32)) multiplexer_8 (
    .in0(x3_q), .in1(Write_Data), .out(multiplexer_8_out), .sel(decoder_1_out3));
  Register #(.width(32)) x3 (.D(multiplexer_8_out), .en(RegWEn), .clk(clk), .Q(x3_q));  // open: clr
  Register #(.width(32)) register_4 (.D(multiplexer_9_out), .en(RegWEn), .clk(clk), .Q(register_4_q));  // open: clr
  Multiplexer #(.enable("false"), .width(32)) multiplexer_9 (
    .in0(register_4_q), .in1(Write_Data), .out(multiplexer_9_out), .sel(decoder_1_out19));
  Multiplexer #(.enable("false"), .width(32)) multiplexer_10 (
    .in0(x4_q), .in1(Write_Data), .out(multiplexer_10_out), .sel(decoder_1_out4));
  Register #(.width(32)) x4 (.D(multiplexer_10_out), .en(RegWEn), .clk(clk), .Q(x4_q));  // open: clr
  Register #(.width(32)) register_5 (.D(multiplexer_11_out), .en(RegWEn), .clk(clk), .Q(register_5_q));  // open: clr
  Multiplexer #(.enable("false"), .width(32)) multiplexer_11 (
    .in0(register_5_q), .in1(Write_Data), .out(multiplexer_11_out), .sel(decoder_1_out20));
  Multiplexer #(.enable("false"), .width(32)) multiplexer_12 (
    .in0(t0), .in1(Write_Data), .out(multiplexer_12_out), .sel(decoder_1_out5));
  Register #(.width(32)) x5 (.D(multiplexer_12_out), .en(RegWEn), .clk(clk), .Q(t0));  // open: clr
  Register #(.width(32)) register_6 (.D(multiplexer_13_out), .en(RegWEn), .clk(clk), .Q(register_6_q));  // open: clr
  Multiplexer #(.enable("false"), .width(32)) multiplexer_13 (
    .in0(register_6_q), .in1(Write_Data), .out(multiplexer_13_out), .sel(decoder_1_out20));
  Multiplexer #(.enable("false"), .width(32)) multiplexer_14 (
    .in0(t1), .in1(Write_Data), .out(multiplexer_14_out), .sel(decoder_1_out6));
  Register #(.width(32)) x6 (.D(multiplexer_14_out), .en(RegWEn), .clk(clk), .Q(t1));  // open: clr
  Register #(.width(32)) register_7 (.D(multiplexer_15_out), .en(RegWEn), .clk(clk), .Q(register_7_q));  // open: clr
  Multiplexer #(.enable("false"), .width(32)) multiplexer_15 (
    .in0(register_7_q), .in1(Write_Data), .out(multiplexer_15_out), .sel(decoder_1_out22));
  Register #(.width(32)) x7 (.D(multiplexer_16_out), .en(RegWEn), .clk(clk), .Q(t2));  // open: clr
  Multiplexer #(.enable("false"), .width(32)) multiplexer_16 (
    .in0(t2), .in1(Write_Data), .out(multiplexer_16_out), .sel(decoder_1_out7));
  Register #(.width(32)) register_8 (.D(multiplexer_17_out), .en(RegWEn), .clk(clk), .Q(register_8_q));  // open: clr
  Multiplexer #(.enable("false"), .width(32)) multiplexer_17 (
    .in0(register_8_q), .in1(Write_Data), .out(multiplexer_17_out), .sel(decoder_1_out23));
  Register #(.width(32)) x8 (.D(multiplexer_18_out), .en(RegWEn), .clk(clk), .Q(s0));  // open: clr
  Multiplexer #(.enable("false"), .width(32)) multiplexer_18 (
    .in0(s0), .in1(Write_Data), .out(multiplexer_18_out), .sel(decoder_1_out8));
  Register #(.width(32)) register_9 (.D(multiplexer_19_out), .en(RegWEn), .clk(clk), .Q(register_9_q));  // open: clr
  Multiplexer #(.enable("false"), .width(32)) multiplexer_19 (
    .in0(register_9_q), .in1(Write_Data), .out(multiplexer_19_out), .sel(decoder_1_out24));
  Register #(.width(32)) x9 (.D(multiplexer_20_out), .en(RegWEn), .clk(clk), .Q(s1));  // open: clr
  Multiplexer #(.enable("false"), .width(32)) multiplexer_20 (
    .in0(s1), .in1(Write_Data), .out(multiplexer_20_out), .sel(decoder_1_out9));
  Multiplexer #(.enable("false"), .width(32)) multiplexer_21 (
    .in0(register_10_q), .in1(Write_Data), .out(multiplexer_21_out), .sel(decoder_1_out25));
  Register #(.width(32)) register_10 (.D(multiplexer_21_out), .en(RegWEn), .clk(clk), .Q(register_10_q));  // open: clr
  Register #(.width(32)) x10 (.D(multiplexer_22_out), .en(RegWEn), .clk(clk), .Q(a0));  // open: clr
  Multiplexer #(.enable("false"), .width(32)) multiplexer_22 (
    .in0(a0), .in1(Write_Data), .out(multiplexer_22_out), .sel(decoder_1_out10));
  Register #(.width(32)) register_11 (.D(multiplexer_23_out), .en(RegWEn), .clk(clk), .Q(register_11_q));  // open: clr
  Multiplexer #(.enable("false"), .width(32)) multiplexer_23 (
    .in0(register_11_q), .in1(Write_Data), .out(multiplexer_23_out), .sel(decoder_1_out26));
  Multiplexer #(.enable("false"), .width(32)) multiplexer_24 (
    .in0(register_12_q), .in1(Write_Data), .out(multiplexer_24_out), .sel(decoder_1_out11));
  Register #(.width(32)) register_12 (.D(multiplexer_24_out), .en(RegWEn), .clk(clk), .Q(register_12_q));  // open: clr
  Register #(.width(32)) register_13 (.D(multiplexer_25_out), .en(RegWEn), .clk(clk), .Q(register_13_q));  // open: clr
  Multiplexer #(.enable("false"), .width(32)) multiplexer_25 (
    .in0(register_13_q), .in1(Write_Data), .out(multiplexer_25_out), .sel(decoder_1_out27));
  Multiplexer #(.enable("false"), .width(32)) multiplexer_26 (
    .in0(register_14_q), .in1(Write_Data), .out(multiplexer_26_out), .sel(decoder_1_out12));
  Register #(.width(32)) register_14 (.D(multiplexer_26_out), .en(RegWEn), .clk(clk), .Q(register_14_q));  // open: clr
  Register #(.width(32)) register_15 (.D(multiplexer_27_out), .en(RegWEn), .clk(clk), .Q(register_15_q));  // open: clr
  Multiplexer #(.enable("false"), .width(32)) multiplexer_27 (
    .in0(register_15_q), .in1(Write_Data), .out(multiplexer_27_out), .sel(decoder_1_out28));
  Multiplexer #(.enable("false"), .width(32)) multiplexer_28 (
    .in0(register_16_q), .in1(Write_Data), .out(multiplexer_28_out), .sel(decoder_1_out13));
  Register #(.width(32)) register_16 (.D(multiplexer_28_out), .en(RegWEn), .clk(clk), .Q(register_16_q));  // open: clr
  Register #(.width(32)) register_17 (.D(multiplexer_29_out), .en(RegWEn), .clk(clk), .Q(register_17_q));  // open: clr
  Multiplexer #(.enable("false"), .width(32)) multiplexer_29 (
    .in0(register_17_q), .in1(Write_Data), .out(multiplexer_29_out), .sel(decoder_1_out29));
  Multiplexer #(.enable("false"), .width(32)) multiplexer_30 (
    .in0(register_18_q), .in1(Write_Data), .out(multiplexer_30_out), .sel(decoder_1_out14));
  Register #(.width(32)) register_18 (.D(multiplexer_30_out), .en(RegWEn), .clk(clk), .Q(register_18_q));  // open: clr
  Register #(.width(32)) register_19 (.D(multiplexer_31_out), .en(RegWEn), .clk(clk), .Q(register_19_q));  // open: clr
  Multiplexer #(.enable("false"), .width(32)) multiplexer_31 (
    .in0(register_19_q), .in1(Write_Data), .out(multiplexer_31_out), .sel(decoder_1_out30));
  Register #(.width(32)) register_20 (.D(multiplexer_32_out), .en(RegWEn), .clk(clk), .Q(register_20_q));  // open: clr
  Multiplexer #(.enable("false"), .width(32)) multiplexer_32 (
    .in0(register_20_q), .in1(Write_Data), .out(multiplexer_32_out), .sel(decoder_1_out15));
  Register #(.width(32)) register_21 (.D(multiplexer_33_out), .en(RegWEn), .clk(clk), .Q(register_21_q));  // open: clr
  Multiplexer #(.enable("false"), .width(32)) multiplexer_33 (
    .in0(register_21_q), .in1(Write_Data), .out(multiplexer_33_out), .sel(decoder_1_out31));

  // Other names for the same wires on the sheet: read_data1[31:0] = Read_Data_1; read_data2[31:0] = Read_Data_2;
  //   read_reg1[4:0] = rs1; read_reg2[4:0] = rs2; write_en = RegWEn; write_reg[4:0] = rd

  // Notes on the sheet:
  //   INPUTS to your circuit
  //   DON'T CHANGE THE LOCATIONS OF THE INPUTS AND OUTPUTS!
  //   These are DEBUG/TEST outputs from your circuit.
  //   OUTPUTS from your circuit
endmodule
